// Logisim project cpu.circ as structural Verilog: 1 circuit, main circuit cpu
module cpu (
  input  jump,
  input  Branch,
  input  RegWrite,
  input  [3:0] MemWrite,
  input  [3:0] MemWriteInst,
  input  MemToReg,
  input  RegDst,
  input  ALUSrc,
  input  [3:0] ALUOp
);

  wire ALU0_zero, and_1_out, clock_1_out;
  wire [4:0] instSplitter_rd, instSplitter_rs, instSplitter_rt, mux2_y;
  wire [15:0] instSplitter_imm16;
  wire [25:0] instSplitter_target26;
  wire [27:0] SXL_2_t28;
  wire [31:0] Adder1_result, Adder_result, ALU0_aluresult, DataMem_memreaddata, InstMem_memreaddata, mux1_y,
       mux3_y, mux4_y, mux_y, PC_pc_out, RegisterFile_readdata1, RegisterFile_readdata2, SE_s32, SHL2_y;

  Clock clock_1 (.out(clock_1_out));
  ProgramCounter PC (.PC_in(mux_y), .PC_out(PC_pc_out));
  Adder_32bit Adder (.A(PC_pc_out), .B(32'h4), .Result(Adder_result));
  mem InstMem (
    .MemAddress(PC_pc_out), .MemWriteMask(MemWriteInst), .clk(clock_1_out), .MemReadData(InstMem_memreaddata));  // open: MemWriteData
  mux2x32 mux (.x0(mux1_y), .x1({Adder_result[31:28], SXL_2_t28}), .Sel(jump), .Y(mux_y));
  SXL2 SXL_2 (.T26(instSplitter_target26), .T28(SXL_2_t28));
  instruction_splitter instSplitter (
    .instruction(InstMem_memreaddata), .target26(instSplitter_target26), .rs(instSplitter_rs),
    .rt(instSplitter_rt), .imm16(instSplitter_imm16), .rd(instSplitter_rd));  // open: op, shamt, func
  mux2x32 mux1 (.x0(Adder_result), .x1(Adder1_result), .Sel(and_1_out), .Y(mux1_y));
  mux2x5 mux2 (.X0(instSplitter_rt), .X1(instSplitter_rd), .Sel(RegDst), .Y(mux2_y));
  SignExtend SE (.S16(instSplitter_imm16), .S32(SE_s32));
  regfile RegisterFile (
    .ReadIndex1(instSplitter_rs), .ReadIndex2(instSplitter_rt), .WriteIndex(mux2_y), .WriteData(mux4_y),
    .RegWEn(RegWrite), .clk(clock_1_out), .ReadData1(RegisterFile_readdata1),
    .ReadData2(RegisterFile_readdata2));
  shiftLeffBy2 SHL2 (.in_1(SE_s32), .Y(SHL2_y));
  mux2x32 mux3 (.x0(RegisterFile_readdata2), .x1(SE_s32), .Sel(ALUSrc), .Y(mux3_y));
  Adder_32bit Adder1 (.A(Adder_result), .B(SHL2_y), .Result(Adder1_result));
  ALU ALU0 (
    .input1(RegisterFile_readdata1), .input2(mux3_y), .ALUOp(ALUOp), .Zero(ALU0_zero),
    .ALUResult(ALU0_aluresult));
  and and_1 (and_1_out, Branch, ALU0_zero);
  mem DataMem (
    .MemAddress(ALU0_aluresult), .MemWriteMask(MemWrite), .MemWriteData(RegisterFile_readdata2),
    .clk(clock_1_out), .MemReadData(DataMem_memreaddata));
  mux2x32 mux4 (.x0(ALU0_aluresult), .x1(DataMem_memreaddata), .Sel(MemToReg), .Y(mux4_y));
endmodule
